# Fritzing sketch TRH (saved by Fritzing 0.9.3b)
circuit board: 8.46667cm x 5.64444cm
breadboards: 2

parts:
  microSD_Transflash1 = SparkFun - microSD Transflash
  R1 = Temperature Sensor (Thermistor) [thermistor_type=NTC package=THT]
  LED1 = LED - 3mm [color="Red (633nm)" package="3 mm [THT]"]
  Bauteil7 = DeadOn RTC - DS3234 Breakout
  Bauteil14 = SHT1x-Breakout
  VCC1 = Battery
  R5 = Temperature Sensor (Thermistor) [thermistor_type=NTC package=THT]
  R6 = Temperature Sensor (Thermistor) [thermistor_type=NTC package=THT]
  LED2 = LED - 3mm [color="Red (633nm)" package="3 mm [THT]"]
  Q1 = TRANSISTOR_NPN [package=to-92]
  Bauteil16 = Arduino Pro Mini v13

nets:
  N1: microSD_Transflash1.DO, Bauteil7.MISO, Bauteil16.D12/MISO
  GND: microSD_Transflash1.GND, LED1.anode, Bauteil14.GND, Q1.C
  N2: microSD_Transflash1.SCK, Bauteil7.SCLK, Bauteil16.D13/SCK
  VCC: microSD_Transflash1.VCC, Bauteil7.VCC, Bauteil14.VCC, R5.pin_0, Bauteil16.VCC
  N3: microSD_Transflash1.DI, Bauteil7.MOSI, Bauteil16.D11_PWM/MOSI
  N4: microSD_Transflash1.CS, Bauteil16.D9_PWM
  N5: R1.pin_0, Bauteil16.D7
  N6: R1.pin_1, LED2.cathode
  N7: LED1.cathode, R5.pin_1, Bauteil16.A0
  GND_2: Bauteil7.GND, VCC1.-, LED2.anode, Q1.E, Bauteil16.GND
  N8: Bauteil7.INT/SQW, Bauteil16.D8
  N9: Bauteil7.SS, Bauteil16.D10_PWM/SS
  N10: Bauteil14.SCK, Bauteil16.D3_PWM
  N11: Bauteil14.DATA, Bauteil16.D5_PWM
  N12: VCC1.+, Bauteil16.RAW
  N13: R6.pin_0, Bauteil16.D4
  N14: R6.pin_1, Q1.B

custom parts:
  DeadOn RTC - DS3234 Breakout: Description: Here is a real time clock based on the DS3234 Real Time Clock IC. The DS3234 is a low-cost, extremely accurate SPI bus real-time clock with an integrated temperature-compensated crystal oscillator and crystal. The RTC maintains seconds, minutes, hours, day, date, month, and year information. The date at the end of the month is automatically adjusted for months with fewer than 31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
  SHT1x-Breakout: The SHT15 Breakout is an easy to use, highly accurate, digital temperature and humidity sensor. This board has been fully calibrated and offers high precision and excellent long-term stability at low cost. The digital CMOSens® technology integrates two sensors and readout circuitry on one single chip. All you need is two lines for 2-wire communication, and you’ll have relative humidity and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
